# Fritzing sketch MYDS (saved by Fritzing 0.9.3b)

parts:
  元件1 = Arduino Uno (Rev3)
  RHT1 = Humidity and Temperature Sensor RHT03
  Y1 = Resonator [package=THT]  # not connected

nets:
  N1: 元件1.D0/RX, RHT1.TXD
  N2: 元件1.D1/TX, RHT1.RXD
  3V3: 元件1.3V3, RHT1.VCC
  GND: 元件1.GND, RHT1.GND

custom parts:
  Humidity and Temperature Sensor RHT03: Digital relative humidity & temperature sensor RHT03
  Resonator: Ceramic resonator with built-in capacitors
